// Logisim project 3Sum8digts.circ as structural Verilog: 1 circuit, main circuit main
module main (
  input  [7:0] A,
  input  [7:0] B,
  input  [7:0] C,
  output [7:0] out_4,
  output [7:0] out_5,
  output [7:0] out_6,
  output [7:0] out_7,
  output [7:0] out_8
);

  wire and_1_out, and_2_out, and_3_out, and_4_out, and_5_out, and_6_out, and_7_out, and_8_out, and_9_out,
       and_10_out, and_11_out, and_12_out, and_13_out, and_14_out, and_15_out, and_16_out, and_17_out,
       and_18_out, and_19_out, and_20_out, and_21_out, and_22_out, and_23_out, and_24_out, and_25_out,
       and_26_out, and_27_out, and_28_out, and_29_out, and_30_out, and_31_out, E0, E1, E2, E3, E4, E5, E6,
       E7, not_1_out, not_2_out, not_3_out, not_4_out, not_5_out, not_6_out, not_7_out, not_8_out, not_9_out,
       not_10_out, not_11_out, not_12_out, not_13_out, not_14_out, not_15_out, not_16_out, not_17_out,
       not_18_out, not_19_out, not_20_out, not_21_out, not_22_out, not_23_out, or_2_out, or_3_out, or_4_out,
       or_8_out, or_10_out, or_11_out, or_12_out, xor_1_out, xor_2_out, xor_3_out, xor_4_out, xor_6_out,
       xor_7_out, xor_8_out, xor_12_out, xor_13_out, xor_15_out, xor_16_out, xor_17_out, xor_18_out,
       xor_19_out, xor_20_out;

  not not_1 (not_1_out, A[0]);
  not not_2 (not_2_out, A[0]);
  not not_3 (not_3_out, A[1]);
  not not_4 (not_4_out, A[1]);
  not not_5 (not_5_out, A[2]);
  not not_6 (not_6_out, A[2]);
  and and_1 (and_1_out, B[0], C[0]);
  and and_2 (and_2_out, not_1_out, C[0]);
  and and_3 (and_3_out, not_2_out, B[0]);
  and and_4 (and_4_out, B[1], C[1]);
  and and_5 (and_5_out, not_3_out, C[1]);
  and and_6 (and_6_out, not_4_out, B[1]);
  not not_7 (not_7_out, A[5]);
  not not_8 (not_8_out, A[5]);
  xor xor_1 (xor_1_out, B[0], C[0]);
  xor xor_2 (xor_2_out, B[1], C[1]);
  xor xor_3 (xor_3_out, B[2], C[2]);
  and and_7 (and_7_out, B[2], C[2]);
  and and_8 (and_8_out, not_5_out, C[2]);
  and and_9 (and_9_out, not_6_out, B[2]);
  xor xor_4 (xor_4_out, B[5], C[5]);
  and and_10 (and_10_out, B[5], C[5]);
  and and_11 (and_11_out, not_7_out, C[5]);
  and and_12 (and_12_out, not_8_out, B[5]);
  xor xor_5 (out_7[0], xor_1_out, A[0]);
  or or_1 (E0, and_1_out, and_2_out, and_3_out);
  xor xor_6 (xor_6_out, xor_2_out, A[1]);
  or or_2 (or_2_out, and_4_out, and_5_out, and_6_out);
  xor xor_7 (xor_7_out, xor_3_out, A[2]);
  or or_3 (or_3_out, and_7_out, and_8_out, and_9_out);
  xor xor_8 (xor_8_out, xor_4_out, A[5]);
  or or_4 (or_4_out, and_10_out, and_11_out, and_12_out);
  not not_9 (not_9_out, xor_6_out);
  not not_10 (not_10_out, xor_7_out);
  not not_11 (not_11_out, xor_8_out);
  xor xor_9 (out_7[1], xor_6_out, E0);
  and and_13 (and_13_out, E0, not_9_out);
  xor xor_10 (out_7[2], xor_7_out, E1);
  and and_14 (and_14_out, E1, not_10_out);
  xor xor_11 (out_7[5], xor_8_out, E4);
  and and_15 (and_15_out, E4, not_11_out);
  not not_12 (not_12_out, A[7]);
  not not_13 (not_13_out, A[7]);
  xor xor_12 (xor_12_out, B[7], C[7]);
  and and_16 (and_16_out, B[7], C[7]);
  and and_17 (and_17_out, not_12_out, C[7]);
  and and_18 (and_18_out, not_13_out, B[7]);
  xor xor_13 (xor_13_out, xor_12_out, A[7]);
  or or_5 (E1, and_13_out, or_2_out);
  or or_6 (E2, and_14_out, or_3_out);
  or or_7 (E5, and_15_out, or_4_out);
  not not_14 (not_14_out, xor_13_out);
  or or_8 (or_8_out, and_16_out, and_17_out, and_18_out);
  xor xor_14 (out_7[7], xor_13_out, E6);
  and and_19 (and_19_out, E6, not_14_out);
  not not_15 (not_15_out, A[3]);
  not not_16 (not_16_out, A[3]);
  not not_17 (not_17_out, A[4]);
  not not_18 (not_18_out, A[4]);
  not not_19 (not_19_out, A[6]);
  not not_20 (not_20_out, A[6]);
  or or_9 (E7, and_19_out, or_8_out);
  xor xor_15 (xor_15_out, B[3], C[3]);
  and and_20 (and_20_out, B[3], C[3]);
  and and_21 (and_21_out, not_15_out, C[3]);
  and and_22 (and_22_out, not_16_out, B[3]);
  xor xor_16 (xor_16_out, B[4], C[4]);
  and and_23 (and_23_out, B[4], C[4]);
  and and_24 (and_24_out, not_17_out, C[4]);
  and and_25 (and_25_out, not_18_out, B[4]);
  xor xor_17 (xor_17_out, B[6], C[6]);
  and and_26 (and_26_out, B[6], C[6]);
  and and_27 (and_27_out, not_19_out, C[6]);
  and and_28 (and_28_out, not_20_out, B[6]);
  xor xor_18 (xor_18_out, xor_15_out, A[3]);
  xor xor_19 (xor_19_out, xor_16_out, A[4]);
  xor xor_20 (xor_20_out, xor_17_out, A[6]);
  not not_21 (not_21_out, xor_18_out);
  or or_10 (or_10_out, and_20_out, and_21_out, and_22_out);
  not not_22 (not_22_out, xor_19_out);
  or or_11 (or_11_out, and_23_out, and_24_out, and_25_out);
  not not_23 (not_23_out, xor_20_out);
  or or_12 (or_12_out, and_26_out, and_27_out, and_28_out);
  xor xor_21 (out_7[3], xor_18_out, E2);
  buf and_29 (and_29_out, E2);  // AND_Gate
  xor xor_22 (out_7[4], xor_19_out, E3);
  and and_30 (and_30_out, E3, not_22_out);
  xor xor_23 (out_7[6], xor_20_out, E5);
  and and_31 (and_31_out, E5, not_23_out);
  or or_13 (E3, and_29_out, or_10_out);
  or or_14 (E4, and_30_out, or_11_out);
  or or_15 (E6, and_31_out, or_12_out);

  assign out_4 = A;
  assign out_5 = B;
  assign out_6 = C;
  assign out_8 = out_7;

  // Other names for the same wires on the sheet: D0 = out_7[0]; D1 = out_7[1]; D2 = out_7[2]; D3 = out_7[3];
  //   D4 = out_7[4]; D5 = out_7[5]; D6 = out_7[6]; D7 = out_7[7]
endmodule
